// Logisim project tn1.circ as structural Verilog: 1 circuit, main circuit main
module main (
  input  A,
  input  B,
  input  A_2,
  input  B_2,
  input  C,
  output out_6,
  output AND,
  output out_8,
  output NAND,
  output NOR,
  output XOR,
  output XNOR,
  output out_13,
  output out_14,
  output out_15
);

  wire nand_2_out;

  and and_1 (AND, A, B);
  not not_1 (out_6, A);
  or or_1 (out_8, A, B);
  nand nand_1 (NAND, A, B);
  nand nand_2 (nand_2_out, A_2, B_2);
  nor nor_1 (NOR, A, B);
  ExactlyOne xor_1 (.out(out_13), .in0(A_2), .in1(B_2), .in2(C));
  xor xor_2 (XOR, A, B);
  nand nand_3 (out_15, nand_2_out, C);
  xnor xnor_1 (XNOR, A, B);
  nand nand_4 (out_14, A_2, B_2, C);

  // Notes on the sheet:
  //   NOT
  //   OR
  //   XOR3
  //   CHAIN
  //   NAND3
endmodule
